# Fritzing sketch Sistema proposto2 (saved by Fritzing 0.9.3b)
breadboards: 3

parts:
  TIP120 = npn-Powertransistor [package="TO220 [THT]"]
  TIP120_2 = npn-Powertransistor [package="TO220 [THT]"]
  TIP120_3 = npn-Powertransistor [package="TO220 [THT]"]
  L4 = Solenoid
  TIP120_4 = npn-Powertransistor [package="TO220 [THT]"]
  TIP120_5 = npn-Powertransistor [package="TO220 [THT]"]
  TIP120_6 = npn-Powertransistor [package="TO220 [THT]"]
  L9 = Solenoid
  TIP120_7 = npn-Powertransistor [package="TO220 [THT]"]
  R1 = Resistor [tolerance=±5% resistance=1k package=THT]
  R2 = Resistor [tolerance=±5% resistance=1k package=THT]
  R3 = Resistor [tolerance=±5% resistance=1k package=THT]
  R4 = Resistor [tolerance=±5% resistance=1k package=THT]
  R5 = Resistor [tolerance=±5% resistance=1k package=THT]
  R6 = Resistor [tolerance=±5% resistance=1k package=THT]
  R7 = Resistor [tolerance=±5% resistance=1k package=THT]
  D1 = Rectifier Diode [part_number=1N4001 package="300 mil [THT]"]
  D3 = Rectifier Diode [part_number=1N4001 package="300 mil [THT]"]
  D4 = Rectifier Diode [part_number=1N4001 package="300 mil [THT]"]
  D6 = Rectifier Diode [part_number=1N4001 package="300 mil [THT]"]
  D7 = Rectifier Diode [part_number=1N4001 package="300 mil [THT]"]
  L10 = Solenoid
  L11 = Solenoid
  L13 = Solenoid
  L14 = Solenoid
  Componente1 = Arduino Mega 2560 (Rev3)
  Power_plug1 = Power plug
  D9 = Rectifier Diode [part_number=1N4001 package="300 mil [THT]"]
  D10 = Rectifier Diode [part_number=1N4001 package="300 mil [THT]"]
  L15 = Solenoid
  MPX1 = MPX2010 pressure sensor [part_number=MPX]

nets:
  N1: TIP120.base, R5.Pin_1
  N2: TIP120.collector, D9.anode, L15.pin1
  N3: TIP120.emitter, TIP120_2.emitter, TIP120_3.emitter, TIP120_4.emitter, TIP120_5.emitter, TIP120_6.emitter, TIP120_7.emitter, Power_plug1.GND
  N4: TIP120_2.base, R4.Pin_1
  N5: TIP120_2.collector, D6.anode, L13.pin1
  N6: TIP120_3.base, R6.Pin_1
  N7: TIP120_3.collector, D7.anode, L14.pin1
  N8: L4.pin1, TIP120_4.collector, D1.anode
  N9: L4.pin2, L9.pin2, D1.cathode, D3.cathode, D4.cathode, D6.cathode, D7.cathode, L10.pin2, L11.pin2, L13.pin2, L14.pin2, Power_plug1.VCC, D9.cathode, D10.cathode, L15.pin2
  N10: TIP120_4.base, R1.Pin_1
  N11: TIP120_5.base, R3.Pin_1
  N12: TIP120_5.collector, D4.anode, L11.pin1
  N13: TIP120_6.base, R2.Pin_1
  N14: TIP120_6.collector, D3.anode, L10.pin1
  N15: L9.pin1, TIP120_7.collector, D10.anode
  N16: TIP120_7.base, R7.Pin_1
  N17: R1.Pin_0, Componente1.D2_PWM
  N18: R2.Pin_0, Componente1.D3_PWM
  N19: R3.Pin_0, Componente1.D4_PWM
  N20: R4.Pin_0, Componente1.D6_PWM
  N21: R5.Pin_0, Componente1.D5_PWM
  N22: R6.Pin_0, Componente1.D7_PWM
  N23: R7.Pin_0, Componente1.D8_PWM
  N24: Componente1.A0, MPX1.GND
  N25: Componente1.5V, MPX1.Vs
  N26: Componente1.GND, MPX1.V_out_-
